# Fritzing sketch eclairage_voiture (saved by Fritzing 0.9.6b)

parts:
  Une_voiture = Arduino Nano (Rev3.0)
  LED1 = LED - 3mm [color="Red (633nm)" current=0.030 package="3 mm [THT]"]
  LED2 = LED - 3mm [color="Red (633nm)" current=0.030 package="3 mm [THT]"]
  LED3 = LED - 3mm [color="White (6500K)" current=0.030 package="3 mm [THT]"]
  LED4 = LED - 3mm [color="White (6500K)" current=0.030 package="3 mm [THT]"]
  LED5 = LED - 3mm [color="Orange (612nm)" current=0.030 package="3 mm [THT]"]
  LED6 = LED - 3mm [color="Orange (612nm)" current=0.030 package="3 mm [THT]"]
  LED7 = LED - 3mm [color="Orange (612nm)" current=0.030 package="3 mm [THT]"]
  LED8 = LED - 3mm [color="Orange (612nm)" current=0.030 package="3 mm [THT]"]
  R2 = Resistor [tolerance=±5% resistance=3.7k power=0.25 package=THT]
  R4 = Resistor [tolerance=±5% resistance=3.7k power=0.25 package=THT]
  R5 = Resistor [tolerance=±5% resistance=3.7k power=0.25 package=THT]
  R6 = Resistor [tolerance=±5% resistance=3.7k power=0.25 package=THT]
  R7 = Resistor [tolerance=±5% resistance=3.7k power=0.25 package=THT]
  R8 = Resistor [tolerance=±5% resistance=3.7k power=0.25 package=THT]
  R1 = Resistor [tolerance=±5% resistance=3.7k power=0.25 package=THT]
  R9 = Resistor [tolerance=±5% resistance=3.7k package="0402 [SMD]"]
  Feux_de_nuit = Arduino Nano (Rev3.0)  # not connected
  Nuit_et_frainage = Arduino Nano (Rev3.0)
  Nuit_freinage_appel_de_phares = Arduino Nano (Rev3.0)
  Stationnement_à_droite_la_nuit = Arduino Nano (Rev3.0)
  Stationnement_à_droite_le_jour = Arduino Nano (Rev3.0)
  Stationnement_droite_+_détresse = Arduino Nano (Rev3.0)
  Nuit_et_feux_de_détresse = Arduino Nano (Rev3.0)
  Tourner_à_droite_la_nuit = Arduino Nano (Rev3.0)
  Deux_véhicules_avec_gyrophare = Arduino Nano (Rev3.0)
  LED9 = LED - 3mm [color="Red (633nm)" current=0.030 package="3 mm [THT]"]
  LED10 = LED - 3mm [color="Red (633nm)" current=0.030 package="3 mm [THT]"]
  LED11 = LED - 3mm [color="White (6500K)" current=0.030 package="3 mm [THT]"]
  LED12 = LED - 3mm [color="White (6500K)" current=0.030 package="3 mm [THT]"]
  LED13 = LED - 3mm [color="Orange (612nm)" current=0.030 package="3 mm [THT]"]
  LED14 = LED - 3mm [color="Orange (612nm)" current=0.030 package="3 mm [THT]"]
  LED15 = LED - 3mm [color="Orange (612nm)" current=0.030 package="3 mm [THT]"]
  LED16 = LED - 3mm [color="Orange (612nm)" current=0.030 package="3 mm [THT]"]  # not connected
  R10 = Resistor [tolerance=±5% resistance=3.7k power=0.25 package=THT]
  R11 = Resistor [tolerance=±5% resistance=3.7k power=0.25 package=THT]
  R12 = Resistor [tolerance=±5% resistance=3.7k power=0.25 package=THT]
  R13 = Resistor [tolerance=±5% resistance=3.7k power=0.25 package=THT]
  R14 = Resistor [tolerance=±5% resistance=3.7k power=0.25 package=THT]
  R15 = Resistor [tolerance=±5% resistance=3.7k power=0.25 package=THT]
  R16 = Resistor [tolerance=±5% resistance=3.7k power=0.25 package=THT]
  R17 = Resistor [tolerance=±5% resistance=3.7k package="0402 [SMD]"]
  LED17 = LED - 3mm [color="Red (633nm)" current=0.030 package="3 mm [THT]"]  # not connected
  LED18 = LED - 3mm [color="Red (633nm)" current=0.030 package="3 mm [THT]"]  # not connected
  LED19 = LED - 3mm [color="White (6500K)" current=0.030 package="3 mm [THT]"]
  LED20 = LED - 3mm [color="White (6500K)" current=0.030 package="3 mm [THT]"]  # not connected
  R18 = Resistor [tolerance=±5% resistance=3.7k power=0.25 package=THT]
  R19 = Resistor [tolerance=±5% resistance=3.7k power=0.25 package=THT]
  R20 = Resistor [tolerance=±5% resistance=3.7k power=0.25 package=THT]
  R21 = Resistor [tolerance=±5% resistance=3.7k power=0.25 package=THT]
  R22 = Resistor [tolerance=±5% resistance=3.7k power=0.25 package=THT]
  Gyrophare = smd LED [color="Orange (612nm)" package="1206 [SMD]"]

nets:
  N1: Une_voiture.GND, Une_voiture.D9, LED1.anode, LED2.anode, LED3.anode, LED4.anode, LED5.anode, LED6.anode, LED7.anode, LED8.anode
  N2: Une_voiture.D2, R7.Pin_0, R9.Pin_0
  N3: Une_voiture.D3, R2.Pin_0, R1.Pin_0
  N4: Une_voiture.D4, R4.Pin_0, R8.Pin_0
  N5: Une_voiture.D5, R5.Pin_0, R6.Pin_0
  N6: Une_voiture.D7, Une_voiture.D8
  N7: Nuit_et_frainage.D7, Nuit_et_frainage.GND
  N8: Nuit_freinage_appel_de_phares.D8, Nuit_freinage_appel_de_phares.GND
  N9: Stationnement_à_droite_la_nuit.D7, Stationnement_à_droite_la_nuit.GND
  N10: Stationnement_à_droite_le_jour.D8, Stationnement_à_droite_le_jour.D9
  N11: Stationnement_droite_+_détresse.D7, Stationnement_droite_+_détresse.GND
  N12: Nuit_et_feux_de_détresse.D9, Nuit_et_feux_de_détresse.GND
  N13: Tourner_à_droite_la_nuit.D8, Tourner_à_droite_la_nuit.GND
  N14: Deux_véhicules_avec_gyrophare.GND, Deux_véhicules_avec_gyrophare.D10, LED9.anode, LED10.anode, LED11.anode, LED12.anode, LED13.anode, LED14.anode, LED15.anode, LED19.anode, Gyrophare.anode
  N15: Deux_véhicules_avec_gyrophare.D2, R12.Pin_0, R17.Pin_0
  N16: Deux_véhicules_avec_gyrophare.D3, R10.Pin_0, R16.Pin_0
  N17: Deux_véhicules_avec_gyrophare.D4, R11.Pin_0, R15.Pin_0
  N18: Deux_véhicules_avec_gyrophare.D5, R13.Pin_0, R14.Pin_0
  N19: Deux_véhicules_avec_gyrophare.D6, R18.Pin_0, R21.Pin_0
  N20: Deux_véhicules_avec_gyrophare.D11/MOSI, R19.Pin_0, R20.Pin_0
  N21: Deux_véhicules_avec_gyrophare.D12/MISO, R22.Pin_0
